// Digital circuit ALU.dig as structural Verilog
module ALU (
  input  in_1,
  input  in_2,
  input  in_3,
  input  [7:0] N,
  input  [7:0] AC,
  input  Shift_Left__Rigth,
  input  [7:0] in_8,
  input  [7:0] in_10,
  input  CLK,
  output out_6,
  output out_9
);

  wire [7:0] divisor8bits_1_p3, divisor8bits_1_p4, mult8bits_1_p3, mult8bits_1_p4, multiplexer_1_out,
       multiplexer_2_out, nand8bits_1_p3, registrador8bits_1_q, registrador8bits_2_q, shift_1_p3,
       somador8bits_1_p4, subtrator8bits_1_p3, xor8bits_1_p3;

  // somador8bits somador8bits_1: pin names not known; wires that end beside it: AC, N, 1'b0, somador8bits_1_p4, out_6
  // subtrator8bits subtrator8bits_1: pin names not known; wires that end beside it: AC, N, subtrator8bits_1_p3, out_9
  // NAND8bits nand8bits_1: pin names not known; wires that end beside it: AC, N, nand8bits_1_p3
  // XOR8bits xor8bits_1: pin names not known; wires that end beside it: AC, N, xor8bits_1_p3
  // divisor8bits divisor8bits_1: pin names not known; wires that end beside it: AC, N, divisor8bits_1_p3, divisor8bits_1_p4
  // shift shift_1: pin names not known; wires that end beside it: Shift_Left__Rigth, AC, shift_1_p3
  // mult8bits mult8bits_1: pin names not known; wires that end beside it: AC, N, mult8bits_1_p3, mult8bits_1_p4
  Multiplexer #(.Selector_Bits(3), .Bits(8)) multiplexer_1 (
    .sel({in_3, in_1, in_2}), .in_0(somador8bits_1_p4), .in_1(subtrator8bits_1_p3), .in_2(nand8bits_1_p3),
    .in_3(xor8bits_1_p3), .in_4(divisor8bits_1_p4), .in_5(shift_1_p3), .in_6(mult8bits_1_p3), .in_7(in_8),
    .out(multiplexer_1_out));
  registrador8bits registrador8bits_1 (.D(multiplexer_1_out), .CLK(CLK), .Q(registrador8bits_1_q));
  Seven_Seg_Hex seven_seg_hex_1 (.d(registrador8bits_1_q[7:4]), .dp(1'b0));
  Multiplexer #(.Selector_Bits(3), .Bits(8)) multiplexer_2 (
    .sel({in_3, in_1, in_2}), .in_0({8{1'b0}}), .in_1({8{1'b0}}), .in_2({8{1'b0}}), .in_3({8{1'b0}}),
    .in_4(divisor8bits_1_p3), .in_5({8{1'b0}}), .in_6(mult8bits_1_p4), .in_7(in_10), .out(multiplexer_2_out));
  Seven_Seg_Hex seven_seg_hex_2 (.d(registrador8bits_1_q[3:0]), .dp(1'b0));
  registrador8bits registrador8bits_2 (.D(multiplexer_2_out), .CLK(CLK), .Q(registrador8bits_2_q));
  Seven_Seg_Hex seven_seg_hex_3 (.d(registrador8bits_2_q[7:4]), .dp(1'b0));
  Seven_Seg_Hex seven_seg_hex_4 (.d(registrador8bits_2_q[3:0]), .dp(1'b0));

  // Notes on the sheet:
  //   AC
  //   MQ
endmodule
