// Digital circuit registrador8bits.dig as structural Verilog
module registrador8bits (
  input  [7:0] D,
  input  CLK,
  output [7:0] Q
);

  D_FF d_ff_1 (.D(D[0]), .C(CLK), .Q(Q[0]));  // open: nQ
  D_FF d_ff_2 (.D(D[1]), .C(CLK), .Q(Q[1]));  // open: nQ
  D_FF d_ff_3 (.D(D[2]), .C(CLK), .Q(Q[2]));  // open: nQ
  D_FF d_ff_4 (.D(D[3]), .C(CLK), .Q(Q[3]));  // open: nQ
  D_FF d_ff_5 (.D(D[4]), .C(CLK), .Q(Q[4]));  // open: nQ
  D_FF d_ff_6 (.D(D[5]), .C(CLK), .Q(Q[5]));  // open: nQ
  D_FF d_ff_7 (.D(D[6]), .C(CLK), .Q(Q[6]));  // open: nQ
  D_FF d_ff_8 (.D(D[7]), .C(CLK), .Q(Q[7]));  // open: nQ

  // Other names for the same wires on the sheet: D_0 = D[0]; D_1 = D[1]; D_2 = D[2]; D_3 = D[3]; D_4 = D[4];
  //   D_5 = D[5]; D_6 = D[6]; D_7 = D[7]; Q_0 = Q[0]; Q_1 = Q[1]; Q_2 = Q[2]; Q_3 = Q[3]; Q_4 = Q[4]; Q_5 = Q[5];
  //   Q_6 = Q[6]; Q_7 = Q[7]
endmodule
